# Fritzing sketch schematic-stripboard (saved by Fritzing 0.9.0b)
stripboards: 1

parts:
  R2 = Resistor [tolerance=±5% resistance=470 package=THT]
  R3 = Resistor [tolerance=±5% resistance=470 package=THT]
  S1 = Pushbutton [package="[THT]"]
  R5 = Resistor [tolerance=±5% resistance=10k package=THT]
  LED1 = LED - 5mm [color="Green (560nm)" package="5 mm [THT]"]
  U1 = 7-SEGMENT-4DIGIT [part_number="Kyx 5461as" package=7-segment-4digit-youngsun]
  U2 = atmega328 [package=dip]
  R6 = Resistor [tolerance=±5% resistance=470 package=THT]
  R1 = Resistor [tolerance=±5% resistance=470 package=THT]
  R4 = Resistor [tolerance=±5% resistance=470 package=THT]
  U3 = Voltage Regulator - 5V [package="TO220 [THT]"]
  VCC1 = Battery block 9V
  C1 = Electrolytic Capacitor [capacitance=10µF package="200 mil [THT, electrolytic]"]
  C2 = Electrolytic Capacitor [capacitance=10µF package="200 mil [THT, electrolytic]"]
  R7 = Resistor [tolerance=±5% resistance=10k package=THT]

nets:
  N1: R2.Pin_0, U1.12
  N2: R2.Pin_1, U2.A5
  N3: R3.Pin_0, U1.9
  N4: R3.Pin_1, U2.A2
  N5: S1.Pin_1, S1.Pin_2, R5.Pin_1, U2.D8
  N6: S1.Pin_3, S1.Pin_4, U2.VCC, U2.AVCC, U3.output_voltage, C2.+, R7.Pin_0
  GND: R5.Pin_0, U2.GND, R1.Pin_1, U3.GND, VCC1.-, C1.-, C2.-
  N7: LED1.cathode, R1.Pin_0
  N8: LED1.anode, U2.D13
  N9: U1.1, U2.D2
  N10: U1.2, U2.D3_(PWM)
  N11: U1.3, U2.D4
  N12: U1.4, U2.D5_(PWM)
  N13: U1.5, U2.D6_(PWM)
  N14: U1.6, R6.Pin_1
  N15: U1.7, U2.A0
  N16: U1.8, R4.Pin_1
  N17: U1.10, U2.A3
  N18: U1.11, U2.A4
  N19: U2.RESET, R7.Pin_1
  N20: U2.D7, R6.Pin_0
  N21: U2.A1, R4.Pin_0
  N22: U3.input_voltage, VCC1.+, C1.+
