# Fritzing sketch schematic (saved by Fritzing 0.9.0b)
breadboards: 1

parts:
  Part1 = Arduino Uno (Rev3)
  U1 = 7-SEGMENT-4DIGIT [part_number="Kyx 5461as" package=7-segment-4digit-youngsun]
  R1 = Resistor [tolerance=±5% resistance=470 package=THT]
  R2 = Resistor [tolerance=±5% resistance=470 package=THT]
  R3 = Resistor [tolerance=±5% resistance=470 package=THT]
  R4 = Resistor [tolerance=±5% resistance=470 package=THT]
  S1 = Pushbutton [package="[THT]"]
  R5 = Resistor [tolerance=±5% resistance=10k package=THT]
  LED1 = LED - 5mm [color="Red (633nm)" package="5 mm [THT]"]
  R6 = Resistor [tolerance=±5% resistance=470 package=THT]

nets:
  N1: Part1.A0, U1.9
  N2: Part1.A1, R2.Pin_1
  N3: Part1.A2, R3.Pin_0
  N4: Part1.A3, U1.14
  N5: Part1.A4/SDA, U1.15
  N6: Part1.A5/SCL, R4.Pin_0
  N7: Part1.D8, S1.Pin_1, S1.Pin_2, R5.Pin_0
  N8: Part1.D13/SCK, LED1.anode
  N9: Part1.D2, U1.2
  N10: Part1.D3_PWM, U1.3
  N11: Part1.D4, U1.4
  N12: Part1.D5_PWM, U1.5
  N13: Part1.D6_PWM, U1.6
  N14: Part1.D7, R1.Pin_1
  N15: Part1.5V, S1.Pin_3, S1.Pin_4
  N16: Part1.GND, R5.Pin_1, R6.Pin_0
  N17: U1.7, R1.Pin_0
  N18: U1.11, R2.Pin_0
  N19: U1.13, R3.Pin_1
  N20: U1.16, R4.Pin_1
  N21: LED1.cathode, R6.Pin_1
